// Logisim project ysyx_F6_minirv_cpu.circ as structural Verilog: 1 circuit, main circuit main
module main (
  input  in_1,
  input  in_2,
  input  in_3,
  output [31:0] out_4,
  output [31:0] out_5
);

  wire add_en, addi_en, clk, comparator_1_eq, comparator_2_eq, comparator_3_eq, comparator_4_eq,
       comparator_5_eq, comparator_6_eq, comparator_7_eq, comparator_8_eq, comparator_9_eq, decoder_1_out1,
       decoder_1_out2, decoder_1_out3, decoder_1_out4, decoder_1_out5, decoder_1_out6, decoder_1_out7,
       decoder_1_out8, decoder_1_out9, decoder_1_out10, decoder_1_out11, decoder_1_out12, decoder_1_out13,
       decoder_1_out14, decoder_1_out15, jalr_en, Lui_en, lw_en, rd_en, rst;
  wire [3:0] rd_sel, rs1_sel, rs2_sel;
  wire [31:0] adder_2_out, adder_3_out, adder_4_out, adder_5_out, and_5_out, bit_extender_7_out,
       bit_extender_8_out, bit_extender_9_out, new_PC_data, PC_data, RAM_addr, RAM_data, register_1_q,
       register_2_q, register_3_q, register_4_q, register_5_q, register_6_q, register_7_q, register_8_q,
       register_9_q, register_10_q, register_11_q, register_12_q, register_13_q, register_14_q,
       register_15_q, register_16_q, register_17_q, rs1, rs2, shifter_1_out, wdata;

  Register #(.width(32)) register_1 (.D(out_4), .en(in_1), .clk(clk), .Q(register_1_q), .clr(rst));
  Bit_Extender #(.in_width(5), .out_width(4), .\type ("zero")) bit_extender_1 (.in(out_5[11:7]), .out(rd_sel));
  Bit_Extender #(.in_width(5), .out_width(4), .\type ("zero")) bit_extender_2 (.in(out_5[19:15]), .out(rs1_sel));
  Comparator #(.mode("unsigned"), .width(7)) comparator_1 (
    .a(out_5[6:0]), .b(7'b0000011), .eq(comparator_1_eq));  // open: gt, lt
  Comparator #(.mode("unsigned"), .width(3)) comparator_2 (
    .a(out_5[14:12]), .b(3'b010), .eq(comparator_2_eq));  // open: gt, lt
  Multiplexer #(.width(32)) multiplexer_1 (.in0(PC_data), .in1(new_PC_data), .out(out_4), .sel(jalr_en));
  Adder #(.width(32)) adder_1 (.a(register_1_q), .b(32'h4), .out(PC_data));  // open: cin, cout
  Bit_Extender #(.in_width(5), .out_width(4), .\type ("zero")) bit_extender_3 (.in(out_5[11:7]), .out(rd_sel));
  Bit_Extender #(.in_width(5), .out_width(4), .\type ("zero")) bit_extender_4 (.in(out_5[19:15]), .out(rs1_sel));
  Bit_Extender #(.in_width(5), .out_width(4), .\type ("zero")) bit_extender_5 (.in(out_5[24:20]), .out(rs2_sel));
  Comparator #(.mode("unsigned"), .width(7)) comparator_3 (
    .a(out_5[6:0]), .b(7'b0010011), .eq(comparator_3_eq));  // open: gt, lt
  Comparator #(.mode("unsigned"), .width(3)) comparator_4 (
    .a(out_5[14:12]), .b(3'b000), .eq(comparator_4_eq));  // open: gt, lt
  Comparator #(.mode("unsigned"), .width(7)) comparator_5 (
    .a(out_5[6:0]), .b(7'b1100111), .eq(comparator_5_eq));  // open: gt, lt
  Comparator #(.mode("unsigned"), .width(3)) comparator_6 (
    .a(out_5[14:12]), .b(3'b000), .eq(comparator_6_eq));  // open: gt, lt
  Comparator #(.mode("unsigned"), .width(7)) comparator_7 (
    .a(out_5[6:0]), .b(7'b0110011), .eq(comparator_7_eq));  // open: gt, lt
  Comparator #(.mode("unsigned"), .width(3)) comparator_8 (
    .a(out_5[14:12]), .b(3'b000), .eq(comparator_8_eq));  // open: gt, lt
  Comparator #(.mode("unsigned"), .width(7)) comparator_9 (
    .a(out_5[31:25]), .b({7{1'b0}}), .eq(comparator_9_eq));  // open: gt, lt
  Comparator #(.mode("unsigned"), .width(7)) comparator_10 (
    .a(out_5[6:0]), .b(7'b0110111), .eq(Lui_en));  // open: gt, lt
  Bit_Extender #(.in_width(5), .out_width(4), .\type ("zero")) bit_extender_6 (.in(out_5[11:7]), .out(rd_sel));
  and and_1 (addi_en, comparator_3_eq, comparator_4_eq);
  and and_2 (jalr_en, comparator_5_eq, comparator_6_eq);
  and and_3 (add_en, comparator_7_eq, comparator_8_eq, comparator_9_eq);
  and and_4 (lw_en, comparator_1_eq, comparator_2_eq);
  ROM #(.addrWidth(6), .dataWidth(32)) rom_1 (.addr(register_1_q[7:2]), .data(out_5));
  assign bit_extender_7_out = {{20{out_5[31]}}, out_5[31:20]};  // Bit_Extender bit_extender_7
  assign bit_extender_8_out = {{20{out_5[31]}}, out_5[31:20]};  // Bit_Extender bit_extender_8
  assign bit_extender_9_out = {{20{out_5[31]}}, out_5[31:20]};  // Bit_Extender bit_extender_9
  assign wdata = lw_en ? RAM_data : 32'bz;  // Controlled_Buffer controlled_buffer_1
  assign wdata = jalr_en ? PC_data : 32'bz;  // Controlled_Buffer controlled_buffer_2
  Adder #(.width(32)) adder_2 (.a(rs1), .b(rs2), .out(adder_2_out));  // open: cin, cout
  Adder #(.width(32)) adder_3 (.a(bit_extender_7_out), .b(rs1), .out(adder_3_out));  // open: cin, cout
  Adder #(.width(32)) adder_4 (.a(bit_extender_8_out), .b(rs1), .out(adder_4_out));  // open: cin, cout
  Adder #(.width(32)) adder_5 (.a(rs1), .b(bit_extender_9_out), .out(adder_5_out));  // open: cin, cout
  assign and_5_out = adder_4_out & 32'hfffffffe;  // AND_Gate and_5, 32 bits wide
  assign wdata = add_en ? adder_2_out : 32'bz;  // Controlled_Buffer controlled_buffer_3
  assign wdata = Lui_en ? {out_5[31:12], {12{1'b0}}} : 32'bz;  // Controlled_Buffer controlled_buffer_4
  assign RAM_addr = lw_en ? adder_5_out : 32'bz;  // Controlled_Buffer controlled_buffer_5
  assign wdata = addi_en ? adder_3_out : 32'bz;  // Controlled_Buffer controlled_buffer_6
  Decoder #(.select(4)) decoder_1 (
    .out1(decoder_1_out1), .out2(decoder_1_out2), .out3(decoder_1_out3), .out4(decoder_1_out4),
    .out5(decoder_1_out5), .out6(decoder_1_out6), .out7(decoder_1_out7), .out8(decoder_1_out8),
    .out9(decoder_1_out9), .out10(decoder_1_out10), .out11(decoder_1_out11), .out12(decoder_1_out12),
    .out13(decoder_1_out13), .out14(decoder_1_out14), .out15(decoder_1_out15), .sel(rd_sel), .en(rd_en));  // open: out0
  assign new_PC_data = jalr_en ? and_5_out : 32'bz;  // Controlled_Buffer controlled_buffer_7
  Register #(.width(32)) register_2 (.D(wdata), .en(1'b0), .clk(clk), .Q(register_2_q), .clr(rst));
  Register #(.width(32)) register_3 (.D(wdata), .en(decoder_1_out8), .clk(clk), .Q(register_3_q), .clr(rst));
  Register #(.width(32)) register_4 (.D(wdata), .en(decoder_1_out1), .clk(clk), .Q(register_4_q), .clr(rst));
  Register #(.width(32)) register_5 (.D(wdata), .en(decoder_1_out9), .clk(clk), .Q(register_5_q), .clr(rst));
  Shifter #(.shift("lr"), .width(32)) shifter_1 (.in(RAM_addr), .\dist (5'b00010), .out(shifter_1_out));
  Register #(.width(32)) register_6 (.D(wdata), .en(decoder_1_out2), .clk(clk), .Q(register_6_q), .clr(rst));
  Register #(.width(32)) register_7 (.D(wdata), .en(decoder_1_out10), .clk(clk), .Q(register_7_q), .clr(rst));
  Register #(.width(32)) register_8 (.D(wdata), .en(decoder_1_out3), .clk(clk), .Q(register_8_q), .clr(rst));
  Register #(.width(32)) register_9 (.D(wdata), .en(decoder_1_out11), .clk(clk), .Q(register_9_q), .clr(rst));
  Button button_1 (.out(rst));
  Clock clock_1 (.out(clk));
  Register #(.width(32)) register_10 (.D(wdata), .en(decoder_1_out4), .clk(clk), .Q(register_10_q), .clr(rst));
  Register #(.width(32)) register_11 (.D(wdata), .en(decoder_1_out12), .clk(clk), .Q(register_11_q), .clr(rst));
  Register #(.width(32)) register_12 (.D(wdata), .en(decoder_1_out5), .clk(clk), .Q(register_12_q), .clr(rst));
  Register #(.width(32)) register_13 (.D(wdata), .en(decoder_1_out13), .clk(clk), .Q(register_13_q), .clr(rst));
  Register #(.width(32)) register_14 (.D(wdata), .en(decoder_1_out6), .clk(clk), .Q(register_14_q), .clr(rst));
  Register #(.width(32)) register_15 (.D(wdata), .en(decoder_1_out14), .clk(clk), .Q(register_15_q), .clr(rst));
  Register #(.width(32)) register_16 (.D(wdata), .en(decoder_1_out7), .clk(clk), .Q(register_16_q), .clr(rst));
  Register #(.width(32)) register_17 (.D(wdata), .en(decoder_1_out15), .clk(clk), .Q(register_17_q), .clr(rst));
  Multiplexer #(.select(4), .width(32)) multiplexer_2 (
    .in0(register_2_q), .in1(register_4_q), .in2(register_6_q), .in3(register_8_q), .in4(register_10_q),
    .in5(register_12_q), .in6(register_14_q), .in7(register_16_q), .in8(register_3_q), .in9(register_5_q),
    .in10(register_7_q), .in11(register_9_q), .in12(register_11_q), .in13(register_13_q),
    .in14(register_15_q), .in15(register_17_q), .out(rs1), .sel(rs1_sel));
  Multiplexer #(.select(4), .width(32)) multiplexer_3 (
    .in0(register_2_q), .in1(register_4_q), .in2(register_6_q), .in3(register_8_q), .in4(register_10_q),
    .in5(register_12_q), .in6(register_14_q), .in7(register_16_q), .in8(register_3_q), .in9(register_5_q),
    .in10(register_7_q), .in11(register_9_q), .in12(register_11_q), .in13(register_13_q),
    .in14(register_15_q), .in15(register_17_q), .out(rs2), .sel(rs2_sel));

  // Other names for the same wires on the sheet: fun3[2:0] = out_5[14:12]; op[31:0] = out_5;
  //   U_type_imme[19:0] = out_5[31:12]; I_type_imme[11:0] = out_5[31:20]; fun7[6:0] = out_5[31:25]; OE_en = in_2;
  //   op_code[6:0] = out_5[6:0]; PC_en = in_1; B0_en = in_3; B1_en = in_3; B2_en = in_3; B3_en = in_3; WE_en = in_3

  // Notes on the sheet:
  //   解码
  //   contents of rom_1 (hex, n*v repeats v):
  //   12345537 543215b7 b50633 c00067
  //   执行
  //   rs1
  //   rs2
endmodule
