// Logisim project ysyx_minirv_cpu.circ as structural Verilog: 1 circuit, main circuit main
module main (
  input  in_1,
  input  in_2,
  output [31:0] out_3,
  output [31:0] out_4,
  output [31:0] out_5,
  output [31:0] out_6
);

  wire add_en, addi_en, B0_en, B1_en, B2_en, B3_en, clk, clock_2_out, comparator_1_eq, comparator_2_eq,
       comparator_3_eq, comparator_4_eq, comparator_5_eq, comparator_6_eq, comparator_7_eq, comparator_8_eq,
       comparator_9_eq, comparator_10_eq, comparator_11_eq, comparator_12_eq, comparator_13_eq,
       comparator_14_eq, comparator_15_eq, comparator_17_lt, comparator_18_lt, decoder_1_out1,
       decoder_1_out2, decoder_1_out3, decoder_1_out4, decoder_1_out5, decoder_1_out6, decoder_1_out7,
       decoder_1_out8, decoder_1_out9, decoder_1_out10, decoder_1_out11, decoder_1_out12, decoder_1_out13,
       decoder_1_out14, decoder_1_out15, decoder_2_out0, decoder_2_out1, decoder_2_out2, decoder_2_out3,
       is_ram, is_vga, jalr_en, lbu_en, Lui_en, lw_en, not_1_out, or_2_out, rd_en, rst, sb_en, sw_en,
       vga_write, WE_en;
  wire [1:0] bit_extender_13_out, bit_extender_18_out;
  wire [3:0] rd_sel, rs1_sel, rs2_sel;
  wire [4:0] bit_extender_14_out, multiplier_1_out;
  wire [7:0] multiplexer_2_out;
  wire [23:0] color;
  wire [31:0] adder_2_out, adder_3_out, adder_4_out, adder_5_out, adder_6_out, adder_7_out, adder_8_out,
       and_10_out, bit_extender_9_out, bit_extender_10_out, bit_extender_11_out, bit_extender_12_out,
       bit_extender_15_out, bit_extender_16_out, bit_extender_17_out, lbu_sel_group, new_PC_data, PC_data,
       RAM_data, register_1_q, register_2_q, register_3_q, register_4_q, register_5_q, register_6_q,
       register_7_q, register_8_q, register_9_q, register_10_q, register_11_q, register_12_q, register_13_q,
       register_14_q, register_15_q, register_16_q, register_17_q, rs1, rs2, sb_sel_group, shifter_1_out,
       shifter_2_out, wdata;

  Register #(.width(32)) register_1 (.D(out_3), .en(in_1), .clk(clk), .Q(register_1_q), .clr(rst));
  Bit_Extender #(.in_width(5), .out_width(4), .\type ("zero")) bit_extender_1 (.in(out_4[11:7]), .out(rd_sel));
  Bit_Extender #(.in_width(5), .out_width(4), .\type ("zero")) bit_extender_2 (.in(out_4[19:15]), .out(rs1_sel));
  Comparator #(.mode("unsigned"), .width(7)) comparator_1 (
    .a(out_4[6:0]), .b(7'b0000011), .eq(comparator_1_eq));  // open: gt, lt
  Comparator #(.mode("unsigned"), .width(3)) comparator_2 (
    .a(out_4[14:12]), .b(3'b010), .eq(comparator_2_eq));  // open: gt, lt
  Comparator #(.mode("unsigned"), .width(7)) comparator_3 (
    .a(out_4[6:0]), .b(7'b0100011), .eq(comparator_3_eq));  // open: gt, lt
  Comparator #(.mode("unsigned"), .width(3)) comparator_4 (
    .a(out_4[14:12]), .b(3'b010), .eq(comparator_4_eq));  // open: gt, lt
  Comparator #(.mode("unsigned"), .width(7)) comparator_5 (
    .a(out_4[6:0]), .b(7'b0000011), .eq(comparator_5_eq));  // open: gt, lt
  Comparator #(.mode("unsigned"), .width(3)) comparator_6 (
    .a(out_4[14:12]), .b(3'b100), .eq(comparator_6_eq));  // open: gt, lt
  Comparator #(.mode("unsigned"), .width(7)) comparator_7 (
    .a(out_4[6:0]), .b(7'b0100011), .eq(comparator_7_eq));  // open: gt, lt
  Comparator #(.mode("unsigned"), .width(3)) comparator_8 (
    .a(out_4[14:12]), .b(3'b000), .eq(comparator_8_eq));  // open: gt, lt
  Multiplexer #(.width(32)) multiplexer_1 (.in0(PC_data), .in1(new_PC_data), .out(out_3), .sel(jalr_en));
  Adder #(.width(32)) adder_1 (.a(register_1_q), .b(32'h4), .out(PC_data));  // open: cin, cout
  Bit_Extender #(.in_width(5), .out_width(4), .\type ("zero")) bit_extender_3 (.in(out_4[11:7]), .out(rd_sel));
  Bit_Extender #(.in_width(5), .out_width(4), .\type ("zero")) bit_extender_4 (.in(out_4[19:15]), .out(rs1_sel));
  Bit_Extender #(.in_width(5), .out_width(4), .\type ("zero")) bit_extender_5 (.in(out_4[24:20]), .out(rs2_sel));
  Bit_Extender #(.in_width(5), .out_width(4), .\type ("zero")) bit_extender_6 (.in(out_4[19:15]), .out(rs1_sel));
  Bit_Extender #(.in_width(5), .out_width(4), .\type ("zero")) bit_extender_7 (.in(out_4[24:20]), .out(rs2_sel));
  Comparator #(.mode("unsigned"), .width(7)) comparator_9 (
    .a(out_4[6:0]), .b(7'b0010011), .eq(comparator_9_eq));  // open: gt, lt
  Comparator #(.mode("unsigned"), .width(3)) comparator_10 (
    .a(out_4[14:12]), .b(3'b000), .eq(comparator_10_eq));  // open: gt, lt
  Comparator #(.mode("unsigned"), .width(7)) comparator_11 (
    .a(out_4[6:0]), .b(7'b1100111), .eq(comparator_11_eq));  // open: gt, lt
  Comparator #(.mode("unsigned"), .width(3)) comparator_12 (
    .a(out_4[14:12]), .b(3'b000), .eq(comparator_12_eq));  // open: gt, lt
  Comparator #(.mode("unsigned"), .width(7)) comparator_13 (
    .a(out_4[6:0]), .b(7'b0110011), .eq(comparator_13_eq));  // open: gt, lt
  Comparator #(.mode("unsigned"), .width(3)) comparator_14 (
    .a(out_4[14:12]), .b(3'b000), .eq(comparator_14_eq));  // open: gt, lt
  Comparator #(.mode("unsigned"), .width(7)) comparator_15 (
    .a(out_4[31:25]), .b({7{1'b0}}), .eq(comparator_15_eq));  // open: gt, lt
  Comparator #(.mode("unsigned"), .width(7)) comparator_16 (
    .a(out_4[6:0]), .b(7'b0110111), .eq(Lui_en));  // open: gt, lt
  Bit_Extender #(.in_width(5), .out_width(4), .\type ("zero")) bit_extender_8 (.in(out_4[11:7]), .out(rd_sel));
  and and_1 (addi_en, comparator_9_eq, comparator_10_eq);
  and and_2 (jalr_en, comparator_11_eq, comparator_12_eq);
  and and_3 (add_en, comparator_13_eq, comparator_14_eq, comparator_15_eq);
  and and_4 (lw_en, comparator_1_eq, comparator_2_eq);
  and and_5 (sw_en, comparator_3_eq, comparator_4_eq);
  and and_6 (lbu_en, comparator_5_eq, comparator_6_eq);
  and and_7 (sb_en, comparator_7_eq, comparator_8_eq);
  ROM #(.addrWidth(24), .dataWidth(32)) rom_1 (.addr(register_1_q[25:2]), .data(out_4));
  assign bit_extender_9_out = {{20{out_4[31]}}, out_4[31:20]};  // Bit_Extender bit_extender_9
  assign bit_extender_10_out = {{20{out_4[31]}}, out_4[31:20]};  // Bit_Extender bit_extender_10
  assign bit_extender_11_out = {{20{out_4[31]}}, out_4[31:20]};  // Bit_Extender bit_extender_11
  assign bit_extender_12_out = {{20{out_4[31]}}, {out_4[31:25], out_4[11:7]}};  // Bit_Extender bit_extender_12
  Bit_Extender #(.in_width(32), .out_width(2), .\type ("zero")) bit_extender_13 (
    .in(lbu_sel_group), .out(bit_extender_13_out));
  Bit_Extender #(.in_width(32), .out_width(5), .\type ("zero")) bit_extender_14 (
    .in(sb_sel_group), .out(bit_extender_14_out));
  assign wdata = jalr_en ? PC_data : 32'bz;  // Controlled_Buffer controlled_buffer_1
  Adder #(.width(32)) adder_2 (.a(rs1), .b(rs2), .out(adder_2_out));  // open: cin, cout
  Adder #(.width(32)) adder_3 (.a(rs1), .b(bit_extender_12_out), .out(adder_3_out));  // open: cin, cout
  assign bit_extender_15_out = {{20{out_4[31]}}, out_4[31:20]};  // Bit_Extender bit_extender_15
  assign bit_extender_16_out = {{20{out_4[31]}}, {out_4[31:25], out_4[11:7]}};  // Bit_Extender bit_extender_16
  Multiplier #(.width(5)) multiplier_1 (
    .a(bit_extender_14_out), .b(5'b01000), .out(multiplier_1_out));  // open: cin, cout
  Adder #(.width(32)) adder_4 (.a(bit_extender_9_out), .b(rs1), .out(adder_4_out));  // open: cin, cout
  Adder #(.width(32)) adder_5 (.a(bit_extender_10_out), .b(rs1), .out(adder_5_out));  // open: cin, cout
  Adder #(.width(32)) adder_6 (.a(rs1), .b(bit_extender_11_out), .out(adder_6_out));  // open: cin, cout
  Adder #(.width(32)) adder_7 (.a(rs1), .b(bit_extender_15_out), .out(adder_7_out));  // open: cin, cout
  assign lbu_sel_group = adder_7_out & 32'h3;  // AND_Gate and_8, 32 bits wide
  Adder #(.width(32)) adder_8 (.a(rs1), .b(bit_extender_16_out), .out(adder_8_out));  // open: cin, cout
  assign sb_sel_group = adder_8_out & 32'h3;  // AND_Gate and_9, 32 bits wide
  assign and_10_out = adder_5_out & 32'hfffffffe;  // AND_Gate and_10, 32 bits wide
  assign wdata = add_en ? adder_2_out : 32'bz;  // Controlled_Buffer controlled_buffer_2
  assign wdata = Lui_en ? {out_4[31:12], {12{1'b0}}} : 32'bz;  // Controlled_Buffer controlled_buffer_3
  assign out_5 = lw_en ? adder_6_out : 32'bz;  // Controlled_Buffer controlled_buffer_4
  assign wdata = lw_en ? RAM_data : 32'bz;  // Controlled_Buffer controlled_buffer_5
  assign out_5 = sw_en ? adder_3_out : 32'bz;  // Controlled_Buffer controlled_buffer_6
  assign out_6 = sw_en ? rs2 : 32'bz;  // Controlled_Buffer controlled_buffer_7
  assign out_5 = lbu_en ? adder_7_out : 32'bz;  // Controlled_Buffer controlled_buffer_8
  Multiplexer #(.select(2), .width(8)) multiplexer_2 (
    .in0(RAM_data[7:0]), .in1(RAM_data[15:8]), .in2(RAM_data[23:16]), .in3(RAM_data[31:24]),
    .out(multiplexer_2_out), .sel(bit_extender_13_out));
  assign out_5 = sb_en ? adder_8_out : 32'bz;  // Controlled_Buffer controlled_buffer_9
  assign wdata = addi_en ? adder_4_out : 32'bz;  // Controlled_Buffer controlled_buffer_10
  assign bit_extender_17_out = {{24{1'b0}}, multiplexer_2_out};  // Bit_Extender bit_extender_17
  Shifter #(.width(32)) shifter_1 (.in(rs2), .\dist (multiplier_1_out), .out(shifter_1_out));
  assign new_PC_data = jalr_en ? and_10_out : 32'bz;  // Controlled_Buffer controlled_buffer_11
  assign wdata = lbu_en ? bit_extender_17_out : 32'bz;  // Controlled_Buffer controlled_buffer_12
  assign out_6 = sb_en ? shifter_1_out : 32'bz;  // Controlled_Buffer controlled_buffer_13
  Button button_1 (.out(rst));
  Clock clock_1 (.out(clk));
  Shifter #(.shift("lr"), .width(32)) shifter_2 (.in(out_5), .\dist (5'b00010), .out(shifter_2_out));
  Decoder #(.select(4)) decoder_1 (
    .out1(decoder_1_out1), .out2(decoder_1_out2), .out3(decoder_1_out3), .out4(decoder_1_out4),
    .out5(decoder_1_out5), .out6(decoder_1_out6), .out7(decoder_1_out7), .out8(decoder_1_out8),
    .out9(decoder_1_out9), .out10(decoder_1_out10), .out11(decoder_1_out11), .out12(decoder_1_out12),
    .out13(decoder_1_out13), .out14(decoder_1_out14), .out15(decoder_1_out15), .sel(rd_sel), .en(rd_en));  // open: out0
  Register #(.width(32)) register_2 (.D(wdata), .en(1'b0), .clk(clk), .Q(register_2_q), .clr(rst));
  Register #(.width(32)) register_3 (.D(wdata), .en(decoder_1_out8), .clk(clk), .Q(register_3_q), .clr(rst));
  RAM #(.addrWidth(24), .asyncread("true"), .byteenables("byteEnables"), .dataWidth(32), .\type ("nonvolatile")) ram_1 (
    .addr(shifter_2_out[23:0]), .we(WE_en), .oe(in_2), .clk(clk), .din(out_6), .dout(RAM_data), .be3(B3_en),
    .be2(B2_en), .be1(B1_en), .be0(B0_en));
  Register #(.width(32)) register_4 (.D(wdata), .en(decoder_1_out1), .clk(clk), .Q(register_4_q), .clr(rst));
  Register #(.width(32)) register_5 (.D(wdata), .en(decoder_1_out9), .clk(clk), .Q(register_5_q), .clr(rst));
  or or_1 (rd_en, addi_en, jalr_en, add_en, Lui_en, lw_en, lbu_en);
  Register #(.width(32)) register_6 (.D(wdata), .en(decoder_1_out2), .clk(clk), .Q(register_6_q), .clr(rst));
  Register #(.width(32)) register_7 (.D(wdata), .en(decoder_1_out10), .clk(clk), .Q(register_7_q), .clr(rst));
  Register #(.width(32)) register_8 (.D(wdata), .en(decoder_1_out3), .clk(clk), .Q(register_8_q), .clr(rst));
  Register #(.width(32)) register_9 (.D(wdata), .en(decoder_1_out11), .clk(clk), .Q(register_9_q), .clr(rst));
  Register #(.width(32)) register_10 (.D(wdata), .en(decoder_1_out4), .clk(clk), .Q(register_10_q), .clr(rst));
  Register #(.width(32)) register_11 (.D(wdata), .en(decoder_1_out12), .clk(clk), .Q(register_11_q), .clr(rst));
  Register #(.width(32)) register_12 (.D(wdata), .en(decoder_1_out5), .clk(clk), .Q(register_12_q), .clr(rst));
  Register #(.width(32)) register_13 (.D(wdata), .en(decoder_1_out13), .clk(clk), .Q(register_13_q), .clr(rst));
  Register #(.width(32)) register_14 (.D(wdata), .en(decoder_1_out6), .clk(clk), .Q(register_14_q), .clr(rst));
  Register #(.width(32)) register_15 (.D(wdata), .en(decoder_1_out14), .clk(clk), .Q(register_15_q), .clr(rst));
  Register #(.width(32)) register_16 (.D(wdata), .en(decoder_1_out7), .clk(clk), .Q(register_16_q), .clr(rst));
  Register #(.width(32)) register_17 (.D(wdata), .en(decoder_1_out15), .clk(clk), .Q(register_17_q), .clr(rst));
  or or_2 (or_2_out, sw_en, sb_en);
  Decoder #(.select(2)) decoder_2 (
    .out0(decoder_2_out0), .out1(decoder_2_out1), .out2(decoder_2_out2), .out3(decoder_2_out3),
    .sel(bit_extender_18_out), .en(sb_en));
  Bit_Extender #(.in_width(32), .out_width(2), .\type ("zero")) bit_extender_18 (
    .in(sb_sel_group), .out(bit_extender_18_out));
  and and_11 (WE_en, or_2_out, is_ram);
  Multiplexer #(.select(4), .width(32)) multiplexer_3 (
    .in0(register_2_q), .in1(register_4_q), .in2(register_6_q), .in3(register_8_q), .in4(register_10_q),
    .in5(register_12_q), .in6(register_14_q), .in7(register_16_q), .in8(register_3_q), .in9(register_5_q),
    .in10(register_7_q), .in11(register_9_q), .in12(register_11_q), .in13(register_13_q),
    .in14(register_15_q), .in15(register_17_q), .out(rs1), .sel(rs1_sel));
  Multiplexer #(.select(4), .width(32)) multiplexer_4 (
    .in0(register_2_q), .in1(register_4_q), .in2(register_6_q), .in3(register_8_q), .in4(register_10_q),
    .in5(register_12_q), .in6(register_14_q), .in7(register_16_q), .in8(register_3_q), .in9(register_5_q),
    .in10(register_7_q), .in11(register_9_q), .in12(register_11_q), .in13(register_13_q),
    .in14(register_15_q), .in15(register_17_q), .out(rs2), .sel(rs2_sel));
  or or_3 (B1_en, sw_en, decoder_2_out1);
  or or_4 (B3_en, sw_en, decoder_2_out3);
  or or_5 (B2_en, decoder_2_out2, sw_en);
  or or_6 (B0_en, decoder_2_out0, sw_en);
  Clock clock_2 (.out(clock_2_out));
  // RGB_Video #(.height(256), .width(256)) rgb_video_1: pin names not known; wires that end beside it: rst, clock_2_out, vga_write, out_5[9:2], out_5[17:10], color, out_5[1:0]
  Comparator #(.mode("unsigned"), .width(32)) comparator_17 (
    .a(out_5), .b(32'h20040000), .lt(comparator_17_lt));  // open: gt, eq
  Comparator #(.mode("unsigned"), .width(32)) comparator_18 (
    .a(out_5), .b(32'h20000000), .lt(comparator_18_lt));  // open: gt, eq
  and and_12 (vga_write, is_vga, sw_en);
  Bit_Extender #(.in_width(32), .out_width(24), .\type ("zero")) bit_extender_19 (.in(out_6), .out(color));
  not not_1 (not_1_out, comparator_18_lt);
  and and_13 (is_vga, comparator_17_lt, not_1_out);
  not not_2 (is_ram, is_vga);

  // Other names for the same wires on the sheet: fun3[2:0] = out_4[14:12]; op[31:0] = out_4;
  //   U_type_imme[19:0] = out_4[31:12]; I_type_imme[11:0] = out_4[31:20]; fun7[6:0] = out_4[31:25];
  //   S_type_imme[11:0] = {out_4[31:25], out_4[11:7]}; mem_data[31:0] = out_6; OE_en = in_2;
  //   op_code[6:0] = out_4[6:0]; PC_en = in_1; RAM_addr[31:0] = out_5; x[7:0] = out_5[9:2]; y[7:0] = out_5[17:10]

  // Notes on the sheet:
  //   I_type
  //   S_type
  //   U_type
  //   S_type
  //   解码
  //   contents of rom_1 (hex, n*v repeats v):
  //   413 93137 10113 10b7 dbc08093 80e7 fe012823 fea10923 fea12423 fe914203 fe4109a3 ff012783 f787b3
  //   f787b3 4b6b7 f0068693 fdc10113 d787b3 10000713 f12423 10593 100793 b00513 2112023 12023 12223 e12623
  //   e12823 f10a23 10b7 a8408093 80e7 2012083 2410113 8067 ff410113 112423 10b7 a7c08093 80e7 513 1800093
  //   80e7 812083 513 c10113 8067 852583 feb12823 fe812e23 3437 a0840413 ff014183 3401b3 1c183 ff114203
  //   440233 24203 4181b3 ff214203 440233 24203 4181b3 ff314203 440233 24203 4181b3 3237 a0020213 320233
  //   24203 ffc12403 420233 420233 410233 11b7 85c18193 fe312823 14800193 fe312623 fec22203 20067 1052703
  //   52683 452783 fe810113 e12423 112a23 fed12823 fef12623 13737 c0070713 fe012223 ff314203 fe4102a3
  //   fef14203 fe410223 fe412203 470233 24203 fe4105a3 ff214203 fe4102a3 fee14203 fe410223 fe412203 470233
  //   24203 fe410523 ff114203 fe4102a3 fed14203 fe410223 fe412203 470233 24203 fe4104a3 ff014203 fe4102a3
  //   fec14203 fe410223 fe412203 470233 24203 fe410423 fe812703 c52603 fee12823 fe812e23 3437 a0840413
  //   ff014183 3401b3 1c183 ff114203 440233 24203 4181b3 ff214203 440233 24203 4181b3 ff314203 440233
  //   24203 4181b3 3237 a0020213 320233 24203 ffc12403 420233 420233 410233 66800193 fe312823 28000193
  //   fe312623 fec22203 20067 c68733 10000513 fe812e23 fe912c23 fee12823 50413 ff012483 fe812423 feb14183
  //   3181b3 fe312423 fe914183 3181b3 fe912423 feb14203 420233 fe412423 fe914203 4181b3 3181b3 fe312a23
  //   fe912423 33237 b0020213 feb14183 4181b3 1c183 fe3103a3 fea14183 4181b3 1c183 fe310323 fe914183
  //   4181b3 1c183 fe3102a3 fe814183 4181b3 1c183 fe310223 ff412183 fe412203 440233 120213 fe412423
  //   feb14203 420233 fe412423 fe914203 4181b3 3237 b0820213 320233 ff812483 ffc12403 24203 420233 420233
  //   410233 11b7 86018193 fe312823 38800193 fe312623 fec22203 20067 812703 10000513 812823 e78733
  //   fe812e23 fe912c23 fee12823 50413 ff012483 fe812423 feb14183 3181b3 fe312423 fe914183 3181b3 fe912423
  //   feb14203 420233 fe412423 fe914203 4181b3 3181b3 fe312a23 fe912423 33237 b0020213 feb14183 4181b3
  //   1c183 fe3103a3 fea14183 4181b3 1c183 fe310323 fe914183 4181b3 1c183 fe3102a3 fe814183 4181b3 1c183
  //   fe310223 ff412183 fe412203 440233 120213 fe412423 feb14203 420233 fe412423 fe914203 4181b3 3237
  //   b0820213 320233 ff812483 ffc12403 24203 420233 420233 410233 11b7 86418193 fe312823 49800193
  //   fe312623 fec22203 20067 8*f787b3 d787b3 f787b3 f787b3 20000437 f40433 812783 c60633 c60633 fef12423
  //   feb14183 3181b3 fe312423 fe914183 fff78213 fe412423 feb14203 420233 fe412423 fe914203 4181b3 3237
  //   b1820213 418233 24203 420233 420233 410233 65800193 fe312823 53c00193 fe312623 fec22203 20067 912623
  //   493 40513 c12223 b12023 10b7 de008093 80e7 12583 412603 812783 148493 40040413 c585b3 fef12823
  //   fe912623 fe812e23 fe912c23 4b437 d0040413 ff014183 340233 100193 320023 fec14183 3401b3 18023 24183
  //   ff114483 940233 100493 920023 fed14483 9404b3 48023 24483 9181b3 ff214483 940233 100493 920023
  //   fee14483 9404b3 48023 24483 9181b3 ff314483 940233 100493 920023 fef14483 9404b3 48023 24483 9181b3
  //   3237 a0020213 320233 24203 ff812483 ffc12403 420233 420233 410233 65400193 fe312823 54400193
  //   fe312623 fec22203 20067 c12483 1012403 1412083 1810113 8067 10000713 fec12823 fee12623 fe812e23
  //   fe912c23 4b437 d0040413 ff014183 340233 100193 320023 fec14183 3401b3 18023 24183 ff114483 940233
  //   100493 920023 fed14483 9404b3 48023 24483 9181b3 ff214483 940233 100493 920023 fee14483 9404b3 48023
  //   24483 9181b3 ff314483 940233 100493 920023 fef14483 9404b3 48023 24483 9181b3 3237 a0020213 320233
  //   24203 ff812483 ffc12403 420233 420233 410233 74c00193 fe312823 28000193 fe312623 fec22203 20067
  //   812703 fee12823 fec12623 fe812e23 fe912c23 4b437 d0040413 ff014183 340233 100193 320023 fec14183
  //   3401b3 18023 24183 ff114483 940233 100493 920023 fed14483 9404b3 48023 24483 9181b3 ff214483 940233
  //   100493 920023 fee14483 9404b3 48023 24483 9181b3 ff314483 940233 100493 920023 fef14483 9404b3 48023
  //   24483 9181b3 3237 a0020213 320233 24203 ff812483 ffc12403 420233 420233 410233 11b7 83418193
  //   fe312823 38800193 fe312623 fec22203 20067 1412083 40637 20000537 1810113 1237 de020213 20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
  //   执行
  //   rs1
  //   rs2
endmodule
